// Digital circuit elevator99.dig as structural Verilog
module elevator99 (
  input  CLK,
  input  RESET,
  input  SWITCH,
  input  [6:0] UP,
  input  [6:0] DOWN,
  input  in_6,
  input  in_7,
  input  in_8,
  input  in_9,
  input  in_10,
  input  in_11,
  input  in_12,
  input  in_13
);

  wire or_1_out, u_fenPin_outclk, u_FSM_f0, u_FSM_f1;
  wire [3:0] u_counter_reset, u_counter_sl_reg;
  wire [6:0] u_clock_sm_seg, u_transcoder_outled, u_transcoderDirect_led_out;
  wire [7:0] u_decode4_8_data_out, u_pulse2level_signalout, u_signalDeal_signal;

  signalDeal #(.applicationType("IVERILOG")) u_signalDeal (
    .upButton(UP), .downButton(DOWN), .stairChooser({in_13, in_12, in_11, in_10, in_9, in_8, in_7, in_6}),
    .rst_n(RESET), .signal(u_signalDeal_signal));
  pulse2level #(.applicationType("IVERILOG")) u_pulse2level (
    .reset(u_decode4_8_data_out), .signalIn(u_signalDeal_signal), .clk(CLK),
    .signalOut(u_pulse2level_signalout));
  fenPin #(.applicationType("IVERILOG")) u_fenPin (.inclk(CLK), .outclk(u_fenPin_outclk));
  FSM #(.applicationType("IVERILOG")) u_FSM (
    .current(u_counter_sl_reg), .signal(u_pulse2level_signalout), .F1(u_FSM_f1), .F0(u_FSM_f0));
  LED _1 (.in(u_pulse2level_signalout[0]));
  LED _2 (.in(u_pulse2level_signalout[1]));
  LED _3 (.in(u_pulse2level_signalout[2]));
  LED _4 (.in(u_pulse2level_signalout[3]));
  LED _5 (.in(u_pulse2level_signalout[4]));
  LED _6 (.in(u_pulse2level_signalout[5]));
  LED _7 (.in(u_pulse2level_signalout[6]));
  LED _8 (.in(u_pulse2level_signalout[7]));
  decode4_8 #(.applicationType("IVERILOG")) u_decode4_8 (.data_in(u_counter_reset), .data_out(u_decode4_8_data_out));
  counter #(.applicationType("IVERILOG")) u_counter (
    .clk(u_fenPin_outclk), .SW0(u_FSM_f0), .SW1(u_FSM_f1), .reset(u_counter_reset), .sl_reg(u_counter_sl_reg));
  transcoder #(.applicationType("IVERILOG")) u_transcoder (
    .value(u_counter_sl_reg), .en(SWITCH), .outled(u_transcoder_outled));
  or or_1 (or_1_out, u_FSM_f0, u_FSM_f1);
  clock #(.applicationType("IVERILOG")) u_clock (
    .show(CLK), .clk(u_fenPin_outclk), .pause(or_1_out), .rst(SWITCH), .sm_seg(u_clock_sm_seg));
  transcoderDirect #(.applicationType("IVERILOG")) u_transcoderDirect (
    .F1(u_FSM_f1), .F0(u_FSM_f0), .en(SWITCH), .led_out(u_transcoderDirect_led_out));
  Seven_Seg seven_seg_1 (
    .a(u_transcoderDirect_led_out[6]), .b(u_transcoderDirect_led_out[5]), .c(u_transcoderDirect_led_out[4]),
    .d(u_transcoderDirect_led_out[3]), .e(u_transcoderDirect_led_out[2]), .f(u_transcoderDirect_led_out[1]),
    .g(u_transcoderDirect_led_out[0]), .dp(1'b0));
  Seven_Seg seven_seg_2 (
    .a(u_clock_sm_seg[6]), .b(u_clock_sm_seg[5]), .c(u_clock_sm_seg[4]), .d(u_clock_sm_seg[3]),
    .e(u_clock_sm_seg[2]), .f(u_clock_sm_seg[1]), .g(u_clock_sm_seg[0]), .dp(1'b0));
  Seven_Seg seven_seg_3 (
    .a(u_transcoder_outled[6]), .b(u_transcoder_outled[5]), .c(u_transcoder_outled[4]),
    .d(u_transcoder_outled[3]), .e(u_transcoder_outled[2]), .f(u_transcoder_outled[1]),
    .g(u_transcoder_outled[0]), .dp(1'b0));

  // Notes on the sheet:
  //   CLK: Hz: 4096
  //   4096HZ
  //   输入要去的楼层
  //   要去的楼层
  //   运行方向
  //   当前楼层
  //   计时器
endmodule

/* Code of signalDeal:
module signalDeal(
    input [6:0] upButton,
    input [7:1] downButton,
    input [7:0] stairChooser,
    input rst_n,
    output reg [7:0] signal
);
// 综合各个输入信号

always @(*)
begin
	if(rst_n)
	begin
	signal <= 8'b00000001;
	end
	else
	begin
		signal <= ({1'b0,upButton}|stairChooser)|{downButton,1'b0};
	end
end
endmodule
*/

/* Code of pulse2level:
module pulse2level(
	input [7:0] reset,
	input [7:0] signalIn,
    input clk,
	output reg [7:0] signalOut
	);

reg [7:0] saver;

always @ (posedge clk) begin
    if(signalIn[0]) saver[0] = 1'b1;
    if(reset[0]) saver[0] = 1'b0;

    if(signalIn[1]) saver[1] = 1'b1;
    if(reset[1]) saver[1] = 1'b0;

    if(signalIn[2]) saver[2] = 1'b1;
    if(reset[2]) saver[2] = 1'b0;

    if(signalIn[3]) saver[3] = 1'b1;
    if(reset[3]) saver[3] = 1'b0;

    if(signalIn[4]) saver[4] = 1'b1;
    if(reset[4]) saver[4] = 1'b0;

    if(signalIn[5]) saver[5] = 1'b1;
    if(reset[5]) saver[5] = 1'b0;

    if(signalIn[6]) saver[6] = 1'b1;
    if(reset[6]) saver[6] = 1'b0;

    if(signalIn[7]) saver[7] = 1'b1;
    if(reset[7]) saver[7] = 1'b0;

    signalOut <= saver;
end

endmodule
*/

/* Code of fenPin:
module fenPin(
    input inclk,
    output outclk
    );
    
    reg [31:0]timeclk;
    
    assign outclk = timeclk[12];
    
    initial begin
    timeclk = 0;
    end
    
    always@(posedge inclk)begin
    timeclk = timeclk +1;
    end

    
endmodule
*/

/* Code of FSM:
module FSM(
	input [3:0] current,
	input [7:0] signal,
	output reg F1,
    output reg F0
	);
	
reg currentF1;
reg currentF0;

initial begin
currentF1=1;
currentF0=0;
end

always @(*)
begin
    case(current)
        4'b0001: if(|signal[7:1]) begin F1 <=1; F0<=0; end   // floor 1
                    else begin F1 <=0; F0<=0; end
        4'b0010: if({currentF1,currentF0}==2'b10) begin
                        if(|signal[7:2]) begin F1 <=1; F0<=0; end   // floor 2
                        else begin 
                        if(|signal[0]) begin F1 <=0; F0<=1; end
                        else begin F1 <=0; F0<=0; end 
                        end
                    end
                 else begin
                        if(|signal[0]) begin F1 <=0; F0<=1; end
                        else begin 
                        if(|signal[7:2]) begin F1 <=1; F0<=0; end
                        else begin F1 <=0; F0<=0; end 
                        end
                    end
        
        4'b0011: if({currentF1,currentF0}==2'b10) begin
                        if(|signal[7:3]) begin F1 <=1; F0<=0; end   // floor 3
                        else begin 
                        if(|signal[1:0]) begin F1 <=0; F0<=1; end
                        else begin F1 <=0; F0<=0; end 
                        end
                    end
                 else begin
                        if(|signal[1:0]) begin F1 <=0; F0<=1; end
                        else begin 
                        if(|signal[7:3]) begin F1 <=1; F0<=0; end
                        else begin F1 <=0; F0<=0; end 
                        end
                    end
        4'b0100: if({currentF1,currentF0}==2'b10) begin
                        if(|signal[7:4]) begin F1 <=1; F0<=0; end   // floor 4
                        else begin 
                        if(|signal[2:0]) begin F1 <=0; F0<=1; end
                        else begin F1 <=0; F0<=0; end 
                        end
                    end
                 else begin
                        if(|signal[2:0]) begin F1 <=0; F0<=1; end
                        else begin 
                        if(|signal[7:4]) begin F1 <=1; F0<=0; end
                        else begin F1 <=0; F0<=0; end 
                        end
                    end
        4'b0101: if({currentF1,currentF0}==2'b10) begin
                        if(|signal[7:5]) begin F1 <=1; F0<=0; end   // floor 5
                        else begin 
                        if(|signal[3:0]) begin F1 <=0; F0<=1; end
                        else begin F1 <=0; F0<=0; end 
                        end
                    end
                 else begin
                        if(|signal[3:0]) begin F1 <=0; F0<=1; end
                        else begin 
                        if(|signal[7:5]) begin F1 <=1; F0<=0; end
                        else begin F1 <=0; F0<=0; end 
                        end
                    end
        4'b0110: if({currentF1,currentF0}==2'b10) begin
                        if(|signal[7:6]) begin F1 <=1; F0<=0; end   // floor 6
                        else begin 
                        if(|signal[4:0]) begin F1 <=0; F0<=1; end
                        else begin F1 <=0; F0<=0; end 
                        end
                    end
                 else begin
                        if(|signal[4:0]) begin F1 <=0; F0<=1; end
                        else begin 
                        if(|signal[7:6]) begin F1 <=1; F0<=0; end
                        else begin F1 <=0; F0<=0; end 
                        end
                    end
        4'b0111: if({currentF1,currentF0}==2'b10) begin
                        if(|signal[7]) begin F1 <=1; F0<=0; end      // floor 7
                        else begin 
                        if(|signal[5:0]) begin F1 <=0; F0<=1; end
                        else begin F1 <=0; F0<=0; end 
                        end
                    end
                 else begin
                        if(|signal[5:0]) begin F1 <=0; F0<=1; end
                        else begin 
                        if(|signal[7]) begin F1 <=1; F0<=0; end
                        else begin F1 <=0; F0<=0; end 
                        end
                    end
        4'b1000: if(|signal[6:0]) begin F1 <=0; F0<=1; end           // floor 8
                    else begin F1 <=0; F0<=0; end
        default: if(|signal[7:1]) begin F1 <=1; F0<=0; end           // floor 1
                    else begin F1 <=0; F0<=0; end
    endcase

    currentF0 <= F0;
    currentF1 <= F1;

end

endmodule
*/

/* Code of decode4_8:
`timescale 10ns/1ns
module decode4_8 (data_out,data_in) ;
input [3:0] data_in;
output [7:0] data_out;
reg [7:0] data_out;
 
always @(data_in)
begin
    case (data_in )
    4'b0001: data_out=8'b00000001;
    4'b0010: data_out=8'b00000010;
    4'b0011: data_out=8'b00000100;
    4'b0100: data_out=8'b00001000;
    4'b0101: data_out=8'b00010000;
    4'b0110: data_out=8'b00100000;
    4'b0111: data_out=8'b01000000;
    4'b1000: data_out=8'b10000000;
    default: data_out=8'b00000000;
    endcase
end
 
endmodule
*/

/* Code of counter:
`timescale 1ns / 1ps
module counter(
    input clk,
    input SW0,
    input SW1,
    output reg [3:0] reset,
    output reg [3:0] sl_reg
);


initial begin
sl_reg = 0;
reset = 0;
end

always @(posedge clk)begin
   case({SW1,SW0})
   2'b01: begin sl_reg=sl_reg-1; reset=sl_reg; end
   2'b10: begin sl_reg=sl_reg+1; reset=sl_reg; end
   default: begin reset = sl_reg; end
   endcase
end

endmodule
*/

/* Code of transcoder:
module transcoder(value,outled,en); 
input [3:0]value;
input en;
output reg [6:0]outled;
//output reg sec=1;
 always @(*) 
 begin 
 if(!en)
 outled=7'b0000000;
 else
case(value) 
4'b0000:outled=7'b0110000;
4'b0001:outled=7'b0110000;
4'b0010:outled=7'b1101101;
4'b0011:outled=7'b1111001;
4'b0100:outled=7'b0110011;
4'b0101:outled=7'b1011011;
4'b0110:outled=7'b1011111;
4'b0111:outled=7'b1110000;
4'b1000:outled=7'b1111111;
4'b1001:outled=7'b1111011;
default:;
 endcase
  end 
 
 endmodule
*/

/* Code of clock:
module clock(
    input show,
    input clk,
    input pause,
    input rst,
    output reg[6:0]sm_seg
    );
    
reg [3:0]timesec0;

initial begin
sm_seg=1;
timesec0=0;
end

always @(posedge clk) begin
        if(pause) begin
            if(timesec0==9) timesec0=0;
        else timesec0=timesec0+1;  
    end
        if(~pause) timesec0=0;
end

always@(posedge show or negedge rst)
begin
    if(!rst)
        begin
        sm_seg = 7'b0000000;
        end
    else
        case(timesec0)
                0:sm_seg= 7'b1111110;                     //显示0
                1:sm_seg= 7'b0110000;                     //显示1
                2:sm_seg= 7'b1101101;                     //显示2
                3:sm_seg= 7'b1111001;                     //显示3
                4:sm_seg= 7'b0110011;                     //显示4
                5:sm_seg= 7'b1011011;                     //显示5
                6:sm_seg= 7'b1011111;                     //显示6
                7:sm_seg= 7'b1110000;                     //显示7
                8:sm_seg= 7'b1111111;                     //显示8
                9:sm_seg= 7'b1111011;                     //显示9
                default:
                sm_seg= 7'b0000000;                        //不显示
        endcase
end
endmodule
*/

/* Code of transcoderDirect:
module transcoderDirect(
	input F1,
        input F0,
	input en,
	output reg [6:0] led_out
	);

always @(*)
begin
if(!en)
led_out=7'b0000000;
else
begin
	case({F1,F0})
		2'b00: led_out = 7'b0000001; //stay
		2'b01: led_out = 7'b0011100; //up
		2'b10: led_out = 7'b1100010; //down
	        default: led_out = 7'b0000001;//stay
	endcase
end
end
endmodule
*/
